// Logisim project digitalClock.circ as structural Verilog
module main (
);

  wire button_1_out, button_2_out, button_3_out, button_4_out, button_5_out, button_6_out, button_7_out,
       button_8_out, button_9_out, button_10_out, button_11_out, button_12_out, button_13_out,
       display_1_alarmflashled, display_1_out_25, display_1_out_26, display_1_out_27, display_1_out_28,
       display_1_out_29, display_1_out_30, display_1_out_31, display_1_out_32, display_1_out_33,
       display_1_out_34, display_1_out_35, display_1_out_36, display_1_out_37, display_1_out_38,
       display_1_out_39, display_1_out_40, display_1_out_41, display_1_out_42, display_1_out_43,
       display_1_out_44, display_1_out_45, display_1_out_46, display_1_out_47, display_1_out_48,
       display_1_out_49, display_1_out_50, display_1_out_51, display_1_out_52, display_1_out_53,
       display_1_out_54, display_1_out_55, display_1_out_56, display_1_out_57, display_1_out_58,
       display_1_out_59, display_1_out_60, display_1_out_61, display_1_out_62, display_1_out_63,
       display_1_out_64, display_1_out_65, display_1_out_66, display_1_out_67, display_1_out_68,
       display_1_out_69, display_1_out_70, display_1_out_71, display_1_out_72, display_1_out_73,
       display_1_out_74, display_1_out_75, display_1_out_76, display_1_out_77, display_1_out_78,
       display_1_out_79, display_1_out_80;
  wire [2:0] display_1_alarmsetled1, display_1_alarmsetled2, display_1_alarmsetled3, display_1_alarmsetled4,
       display_1_alarmsetled5, display_1_alarmsetled6, display_1_alarmsetled7, display_1_alarmsetled8,
       display_1_alarmsetled9, display_1_alarmsetled10;

  instructions instructions_1 ();
  Button button_1 (.out(button_1_out));
  Button button_2 (.out(button_2_out));
  Button button_3 (.out(button_3_out));
  Button button_4 (.out(button_4_out));
  Button button_5 (.out(button_5_out));
  LED led_1 (.in(display_1_alarmflashled));
  _7_Segment_Display u_7_segment_display_1 (
    .g(display_1_out_25), .f(display_1_out_26), .a(display_1_out_27), .b(display_1_out_28),
    .e(display_1_out_53), .d(display_1_out_54), .c(display_1_out_55), .dp(display_1_out_56));
  _7_Segment_Display u_7_segment_display_2 (
    .g(display_1_out_29), .f(display_1_out_30), .a(display_1_out_31), .b(display_1_out_32),
    .e(display_1_out_57), .d(display_1_out_58), .c(display_1_out_59), .dp(display_1_out_60));
  Button button_6 (.out(button_6_out));
  _7_Segment_Display u_7_segment_display_3 (
    .g(display_1_out_33), .f(display_1_out_34), .a(display_1_out_35), .b(display_1_out_36),
    .e(display_1_out_61), .d(display_1_out_62), .c(display_1_out_63), .dp(display_1_out_64));
  Button button_7 (.out(button_7_out));
  Button button_8 (.out(button_8_out));
  _7_Segment_Display u_7_segment_display_4 (
    .g(display_1_out_37), .f(display_1_out_38), .a(display_1_out_39), .b(display_1_out_40),
    .e(display_1_out_65), .d(display_1_out_66), .c(display_1_out_67), .dp(display_1_out_68));
  _7_Segment_Display u_7_segment_display_5 (
    .g(display_1_out_41), .f(display_1_out_42), .a(display_1_out_43), .b(display_1_out_44),
    .e(display_1_out_69), .d(display_1_out_70), .c(display_1_out_71), .dp(display_1_out_72));
  display display_1 (
    .out_25(display_1_out_25), .out_53(display_1_out_53), .out_26(display_1_out_26),
    .out_54(display_1_out_54), .out_27(display_1_out_27), .out_55(display_1_out_55),
    .out_28(display_1_out_28), .out_56(display_1_out_56), .out_29(display_1_out_29),
    .out_57(display_1_out_57), .out_30(display_1_out_30), .out_58(display_1_out_58),
    .out_31(display_1_out_31), .out_59(display_1_out_59), .out_32(display_1_out_32),
    .out_60(display_1_out_60), .out_33(display_1_out_33), .out_61(display_1_out_61),
    .out_34(display_1_out_34), .out_62(display_1_out_62), .out_35(display_1_out_35),
    .out_63(display_1_out_63), .out_36(display_1_out_36), .out_64(display_1_out_64),
    .out_37(display_1_out_37), .out_65(display_1_out_65), .out_38(display_1_out_38),
    .out_66(display_1_out_66), .out_39(display_1_out_39), .out_67(display_1_out_67),
    .out_40(display_1_out_40), .out_68(display_1_out_68), .out_41(display_1_out_41),
    .out_69(display_1_out_69), .out_42(display_1_out_42), .out_70(display_1_out_70),
    .out_43(display_1_out_43), .out_71(display_1_out_71), .out_44(display_1_out_44),
    .out_72(display_1_out_72), .alarmflashLED(display_1_alarmflashled),
    .alarmsetLED1(display_1_alarmsetled1), .alarmsetLED2(display_1_alarmsetled2),
    .alarmsetLED3(display_1_alarmsetled3), .alarmsetLED4(display_1_alarmsetled4),
    .alarmsetLED5(display_1_alarmsetled5), .alarmsetLED6(display_1_alarmsetled6),
    .alarmsetLED7(display_1_alarmsetled7), .alarmsetLED8(display_1_alarmsetled8),
    .alarmsetLED9(display_1_alarmsetled9), .alarmsetLED10(display_1_alarmsetled10),
    .out_45(display_1_out_45), .out_73(display_1_out_73), .out_46(display_1_out_46),
    .out_74(display_1_out_74), .out_47(display_1_out_47), .out_75(display_1_out_75),
    .out_48(display_1_out_48), .out_76(display_1_out_76), .out_49(display_1_out_49),
    .out_77(display_1_out_77), .out_50(display_1_out_50), .out_78(display_1_out_78),
    .out_51(display_1_out_51), .out_79(display_1_out_79), .out_52(display_1_out_52),
    .out_80(display_1_out_80), .SET(button_12_out), .RESET(button_13_out), .alarm_button(button_3_out),
    .countup_button(button_4_out), .countdown_button(button_5_out), .ADDS0(button_11_out),
    .ADDS1(button_10_out), .ADDM0(button_9_out), .ADDM1(button_8_out), .ADDH0(button_7_out),
    .ADDH1(button_6_out), .twentyfour(button_1_out), .twelve(button_2_out));
  Button button_9 (.out(button_9_out));
  _7_Segment_Display u_7_segment_display_6 (
    .g(display_1_out_45), .f(display_1_out_46), .a(display_1_out_47), .b(display_1_out_48),
    .e(display_1_out_73), .d(display_1_out_74), .c(display_1_out_75), .dp(display_1_out_76));
  Button button_10 (.out(button_10_out));
  Button button_11 (.out(button_11_out));
  _7_Segment_Display u_7_segment_display_7 (
    .g(display_1_out_49), .f(display_1_out_50), .a(display_1_out_51), .b(display_1_out_52),
    .e(display_1_out_77), .d(display_1_out_78), .c(display_1_out_79), .dp(display_1_out_80));
  DotMatrix #(.matrixcols(10), .matrixrows(3)) dotmatrix_1 (
    .col0(display_1_alarmsetled1), .col1(display_1_alarmsetled2), .col2(display_1_alarmsetled3),
    .col3(display_1_alarmsetled4), .col4(display_1_alarmsetled5), .col5(display_1_alarmsetled6),
    .col6(display_1_alarmsetled7), .col7(display_1_alarmsetled8), .col8(display_1_alarmsetled9),
    .col9(display_1_alarmsetled10));
  Button button_12 (.out(button_12_out));
  Button button_13 (.out(button_13_out));
endmodule

module display (
  input  twentyfour,
  input  twelve,
  input  alarm_button,
  input  countup_button,
  input  countdown_button,
  input  ADDS0,
  input  ADDS1,
  input  ADDM0,
  input  ADDM1,
  input  ADDH0,
  input  ADDH1,
  input  SET,
  input  RESET,
  output alarmflashLED,
  output [2:0] alarmsetLED1,
  output [2:0] alarmsetLED2,
  output [2:0] alarmsetLED3,
  output [2:0] alarmsetLED4,
  output [2:0] alarmsetLED5,
  output [2:0] alarmsetLED6,
  output [2:0] alarmsetLED7,
  output [2:0] alarmsetLED8,
  output [2:0] alarmsetLED9,
  output [2:0] alarmsetLED10,
  output out_25,
  output out_26,
  output out_27,
  output out_28,
  output out_29,
  output out_30,
  output out_31,
  output out_32,
  output out_33,
  output out_34,
  output out_35,
  output out_36,
  output out_37,
  output out_38,
  output out_39,
  output out_40,
  output out_41,
  output out_42,
  output out_43,
  output out_44,
  output out_45,
  output out_46,
  output out_47,
  output out_48,
  output out_49,
  output out_50,
  output out_51,
  output out_52,
  output out_53,
  output out_54,
  output out_55,
  output out_56,
  output out_57,
  output out_58,
  output out_59,
  output out_60,
  output out_61,
  output out_62,
  output out_63,
  output out_64,
  output out_65,
  output out_66,
  output out_67,
  output out_68,
  output out_69,
  output out_70,
  output out_71,
  output out_72,
  output out_73,
  output out_74,
  output out_75,
  output out_76,
  output out_77,
  output out_78,
  output out_79,
  output out_80
);

  wire and_1_out, and_2_out, and_3_out, and_4_out, and_5_out, and_6_out, and_7_out, and_8_out, and_9_out,
       and_10_out, and_11_out, and_12_out, and_13_out, and_14_out, and_15_out, and_16_out, decoder_1_out2,
       decoder_1_out3, decoder_1_out4;
  wire [2:0] mode;
  wire [27:0] BOT12, BOT24, BOTALARM, BOTDOWN, BOTUP, TOP12, TOP24, TOPALARM, TOPDOWN, TOPUP;

  Decoder #(.enable("false"), .select(3)) decoder_1 (
    .out2(decoder_1_out2), .out3(decoder_1_out3), .out4(decoder_1_out4), .sel(mode));  // open: out0, out1, out5, out6, out7
  modeselect modeselect_1 (
    .twentyfour(twentyfour), .twelve(twelve), .alarm_button(alarm_button), .countup_button(countup_button),
    .countdown_button(countdown_button), .out_6(mode));
  and and_1 (and_1_out, decoder_1_out2, ADDS0);
  and and_2 (and_2_out, decoder_1_out2, ADDS1);
  and and_3 (and_3_out, decoder_1_out2, ADDM0);
  and and_4 (and_4_out, decoder_1_out2, ADDM1);
  and and_5 (and_5_out, decoder_1_out2, ADDH0);
  and and_6 (and_6_out, decoder_1_out2, ADDH1);
  and and_7 (and_7_out, decoder_1_out4, SET);
  and and_8 (and_8_out, decoder_1_out4, ADDS0);
  and and_9 (and_9_out, decoder_1_out4, ADDS1);
  and and_10 (and_10_out, decoder_1_out4, ADDM0);
  and and_11 (and_11_out, decoder_1_out4, ADDM1);
  and and_12 (and_12_out, decoder_1_out4, ADDH0);
  and and_13 (and_13_out, decoder_1_out4, ADDH1);
  and and_14 (and_14_out, decoder_1_out4, RESET);
  and and_15 (and_15_out, SET, decoder_1_out3);
  and and_16 (and_16_out, decoder_1_out3, RESET);
  alarm alarm_1 (
    .ADDS0(and_1_out), .ADDS1(and_2_out), .ADDM0(and_3_out), .ADDM1(and_4_out), .ADDH0(and_5_out),
    .ADDH1(and_6_out), .TOP(TOPALARM), .BOTTOM(BOTALARM));
  countdown countdown_1 (
    .START(and_7_out), .ADDS0(and_8_out), .ADDS1(and_9_out), .ADDM0(and_10_out), .ADDM1(and_11_out),
    .ADDH0(and_12_out), .ADDH1(and_13_out), .STOP(and_14_out), .TOP(TOPDOWN), .BOTTOM(BOTDOWN));
  clock24and12 clock24and12_1 (.TOP24(TOP24), .TOP12(TOP12), .BOTTOM24(BOT24), .BOTTOM12(BOT12));
  countup countup_1 (.START(and_15_out), .STOP(and_16_out), .TOP(TOPUP), .BOTTOM(BOTUP));
  Multiplexer #(.select(3), .width(28)) multiplexer_1 (
    .in0(TOP24), .in1(TOP12), .in2(TOPALARM), .in3(TOPUP), .in4(TOPDOWN),
    .out({out_25, out_26, out_27, out_28, out_29, out_30, out_31, out_32, out_33, out_34, out_35, out_36, out_37, out_38, out_39, out_40, out_41, out_42, out_43, out_44, out_45, out_46, out_47, out_48, out_49, out_50, out_51, out_52}),
    .sel(mode));  // open: in5, in6, in7
  Multiplexer #(.select(3), .width(28)) multiplexer_2 (
    .in0(BOT24), .in1(BOT12), .in2(BOTALARM), .in3(BOTUP), .in4(BOTDOWN),
    .out({out_53, out_54, out_55, out_56, out_57, out_58, out_59, out_60, out_61, out_62, out_63, out_64, out_65, out_66, out_67, out_68, out_69, out_70, out_71, out_72, out_73, out_74, out_75, out_76, out_77, out_78, out_79, out_80}),
    .sel(mode));  // open: in5, in6, in7
  alarmled alarmled_1 (
    .RESET(RESET), .TOPCLOCK(TOP24), .TOPALARM(TOPALARM), .BOTTOMALARM(BOTALARM), .BOTTOMCLOCK(BOT24),
    .SET(SET), .MODE(mode), .LEDFLASH(alarmflashLED), .alarmset(alarmsetLED1));

  assign alarmsetLED2 = alarmsetLED1;
  assign alarmsetLED3 = alarmsetLED1;
  assign alarmsetLED4 = alarmsetLED1;
  assign alarmsetLED5 = alarmsetLED1;
  assign alarmsetLED6 = alarmsetLED1;
  assign alarmsetLED7 = alarmsetLED1;
  assign alarmsetLED8 = alarmsetLED1;
  assign alarmsetLED9 = alarmsetLED1;
  assign alarmsetLED10 = alarmsetLED1;
endmodule

module modeselect (
  input  twentyfour,
  input  twelve,
  input  alarm_button,
  input  countup_button,
  input  countdown_button,
  output [2:0] out_6
);

  wire or_1_out, or_2_out, or_3_out, or_4_out, or_5_out;

  S_R_Flip_Flop #(.trigger("high")) s_r_ff_1 (
    .S(countdown_button), .R(or_1_out), .clk(1'b1), .Q(out_6[2]));  // open: reset, Qn, preset
  or or_1 (or_1_out, twelve, twentyfour, alarm_button, countup_button);
  or or_2 (or_2_out, alarm_button, countup_button);
  S_R_Flip_Flop #(.trigger("high")) s_r_ff_2 (
    .S(or_2_out), .R(or_3_out), .clk(1'b1), .Q(out_6[1]));  // open: reset, Qn, preset
  or or_3 (or_3_out, twelve, twentyfour, countdown_button);
  or or_4 (or_4_out, twelve, countup_button);
  or or_5 (or_5_out, twentyfour, alarm_button, countdown_button);
  S_R_Flip_Flop #(.trigger("high")) s_r_ff_3 (
    .S(or_4_out), .R(or_5_out), .clk(1'b1), .Q(out_6[0]));  // open: reset, Qn, preset

  // Other names for the same wires on the sheet: alarm = alarm_button; countdown = countdown_button;
  //   countup = countup_button
endmodule

module clock24and12 (
  output [27:0] TOP24,
  output [27:0] TOP12,
  output [27:0] BOTTOM24,
  output [27:0] BOTTOM12
);

  wire and_1_out, clock_1_out, mod2_1_overflow, mod3_1_overflow, mod6_1_overflow, mod6_2_overflow,
       mod10_1_overflow, mod10_2_overflow, mod10_3_overflow, mod10alt_1_overflow, or_1_out;
  wire [3:0] mod2_1_q, mod3_1_q, mod6_1_q, mod6_2_q, mod10_1_q, mod10_2_q, mod10_3_q, mod10alt_1_q,
       multiplexer_1_out, multiplexer_2_out;

  Clock clock_1 (.out(clock_1_out));
  MOD10 mod10_1 (.X(1'b0), .CLK(clock_1_out), .Q(mod10_1_q), .Overflow(mod10_1_overflow));
  MOD6 mod6_1 (.CLK(mod10_1_overflow), .Q(mod6_1_q), .Overflow(mod6_1_overflow));
  MOD10 mod10_2 (.X(1'b0), .CLK(mod6_1_overflow), .Q(mod10_2_q), .Overflow(mod10_2_overflow));
  MOD6 mod6_2 (.CLK(mod10_2_overflow), .Q(mod6_2_q), .Overflow(mod6_2_overflow));
  MOD10 mod10_3 (.X(mod3_1_overflow), .CLK(mod6_2_overflow), .Q(mod10_3_q), .Overflow(mod10_3_overflow));
  MOD3 mod3_1 (.CLK(mod10_3_overflow), .Q(mod3_1_q), .Overflow(mod3_1_overflow));
  MOD10alt mod10alt_1 (.X(mod2_1_overflow), .CLK(mod6_2_overflow), .Q(mod10alt_1_q), .Overflow(mod10alt_1_overflow));
  MOD2 mod2_1 (.CLK(mod10alt_1_overflow), .Q(mod2_1_q), .OVERFLOW(mod2_1_overflow));
  Multiplexer #(.width(4)) multiplexer_1 (.in0(4'b0010), .in1(mod10alt_1_q), .out(multiplexer_1_out), .sel(or_1_out));
  or or_1 (or_1_out, mod10alt_1_q[0], mod10alt_1_q[1], mod10alt_1_q[2], mod10alt_1_q[3], mod2_1_q[0], mod2_1_q[1], mod2_1_q[2], mod2_1_q[3]);
  and and_1 (and_1_out, mod10alt_1_overflow, mod2_1_overflow);
  Multiplexer #(.width(4)) multiplexer_2 (.in0(4'b0001), .in1(mod2_1_q), .out(multiplexer_2_out), .sel(or_1_out));
  T_Flip_Flop t_ff_1 (.T(1'b1), .clk(and_1_out), .Qn(BOTTOM12[1]));  // open: Q, reset, preset
  // BCD_to_7_Segment_decoder bcd_to_7_segment_decoder_1: pin names not known
  // BCD_to_7_Segment_decoder bcd_to_7_segment_decoder_2: pin names not known; wires that end beside it: multiplexer_1_out, multiplexer_2_out
  // BCD_to_7_Segment_decoder bcd_to_7_segment_decoder_3: pin names not known
  // BCD_to_7_Segment_decoder bcd_to_7_segment_decoder_4: pin names not known; wires that end beside it: mod10_1_q
  // BCD_to_7_Segment_decoder bcd_to_7_segment_decoder_5: pin names not known; wires that end beside it: mod6_1_q
  // BCD_to_7_Segment_decoder bcd_to_7_segment_decoder_6: pin names not known; wires that end beside it: mod10_2_q
  // BCD_to_7_Segment_decoder bcd_to_7_segment_decoder_7: pin names not known; wires that end beside it: mod6_2_q
  // BCD_to_7_Segment_decoder bcd_to_7_segment_decoder_8: pin names not known; wires that end beside it: mod10_3_q, mod3_1_q

  assign {BOTTOM12[24], BOTTOM12[20], BOTTOM12[16], BOTTOM12[12], BOTTOM12[8], BOTTOM12[4:2], BOTTOM12[0]} = 9'ha4;
  assign {BOTTOM24[24], BOTTOM24[20:0]} = {2'b01, BOTTOM12[19:17], 1'b0, BOTTOM12[15:13], 1'b1, BOTTOM12[11:9], 1'b0, BOTTOM12[7:5], {5{1'b0}}};
  assign TOP12[3:0] = 4'b1111;
  assign TOP24[19:0] = {TOP12[19:4], 4'b0000};
endmodule

module alarm (
  input  ADDS0,
  input  ADDS1,
  input  ADDM0,
  input  ADDM1,
  input  ADDH0,
  input  ADDH1,
  output [27:0] TOP,
  output [27:0] BOTTOM
);

  wire and_1_out, and_2_out, and_3_out, and_4_out, and_5_out, and_6_out, and_7_out, or_1_out, or_2_out,
       T0_qn, T1_qn, T2_qn, t_ff_1_qn, t_ff_2_qn, t_ff_3_qn, t_ff_4_qn, t_ff_5_qn, t_ff_6_qn, t_ff_7_qn,
       t_ff_8_qn, t_ff_9_qn, t_ff_11_qn, t_ff_12_qn, t_ff_13_qn, t_ff_14_qn;
  wire [1:0] t_ff_5_q;
  wire [3:0] T0_q, t_ff_1_q, t_ff_2_q, t_ff_3_q, t_ff_4_q;

  T_Flip_Flop T0 (.T(1'b1), .clk(ADDS0), .Q(T0_q[0]), .Qn(T0_qn), .reset(and_2_out));  // open: preset
  T_Flip_Flop t_ff_1 (.T(1'b1), .clk(ADDS1), .Q(t_ff_1_q[0]), .Qn(t_ff_1_qn), .reset(and_3_out));  // open: preset
  T_Flip_Flop t_ff_2 (.T(1'b1), .clk(ADDM0), .Q(t_ff_2_q[0]), .Qn(t_ff_2_qn), .reset(and_4_out));  // open: preset
  T_Flip_Flop t_ff_3 (.T(1'b1), .clk(ADDM1), .Q(t_ff_3_q[0]), .Qn(t_ff_3_qn), .reset(and_5_out));  // open: preset
  T_Flip_Flop t_ff_4 (.T(1'b1), .clk(ADDH0), .Q(t_ff_4_q[0]), .Qn(t_ff_4_qn), .reset(or_2_out));  // open: preset
  T_Flip_Flop t_ff_5 (.T(1'b1), .clk(ADDH1), .Q(t_ff_5_q[0]), .Qn(t_ff_5_qn), .reset(and_1_out));  // open: preset
  T_Flip_Flop T1 (.T(1'b1), .clk(T0_qn), .Q(T0_q[1]), .Qn(T1_qn), .reset(and_2_out));  // open: preset
  T_Flip_Flop t_ff_6 (.T(1'b1), .clk(t_ff_1_qn), .Q(t_ff_1_q[1]), .Qn(t_ff_6_qn), .reset(and_3_out));  // open: preset
  T_Flip_Flop t_ff_7 (.T(1'b1), .clk(t_ff_2_qn), .Q(t_ff_2_q[1]), .Qn(t_ff_7_qn), .reset(and_4_out));  // open: preset
  T_Flip_Flop t_ff_8 (.T(1'b1), .clk(t_ff_3_qn), .Q(t_ff_3_q[1]), .Qn(t_ff_8_qn), .reset(and_5_out));  // open: preset
  T_Flip_Flop t_ff_9 (.T(1'b1), .clk(t_ff_4_qn), .Q(t_ff_4_q[1]), .Qn(t_ff_9_qn), .reset(or_2_out));  // open: preset
  T_Flip_Flop t_ff_10 (.T(1'b1), .clk(t_ff_5_qn), .Q(t_ff_5_q[1]), .reset(and_1_out));  // open: Qn, preset
  T_Flip_Flop T2 (.T(1'b1), .clk(T1_qn), .Q(T0_q[2]), .Qn(T2_qn), .reset(and_2_out));  // open: preset
  T_Flip_Flop t_ff_11 (.T(1'b1), .clk(t_ff_6_qn), .Q(t_ff_1_q[2]), .Qn(t_ff_11_qn), .reset(and_3_out));  // open: preset
  T_Flip_Flop t_ff_12 (.T(1'b1), .clk(t_ff_7_qn), .Q(t_ff_2_q[2]), .Qn(t_ff_12_qn), .reset(and_4_out));  // open: preset
  T_Flip_Flop t_ff_13 (.T(1'b1), .clk(t_ff_8_qn), .Q(t_ff_3_q[2]), .Qn(t_ff_13_qn), .reset(and_5_out));  // open: preset
  T_Flip_Flop t_ff_14 (.T(1'b1), .clk(t_ff_9_qn), .Q(t_ff_4_q[2]), .Qn(t_ff_14_qn), .reset(or_2_out));  // open: preset
  T_Flip_Flop T3 (.T(1'b1), .clk(T2_qn), .Q(T0_q[3]), .reset(and_2_out));  // open: Qn, preset
  T_Flip_Flop t_ff_15 (.T(1'b1), .clk(t_ff_11_qn), .Q(t_ff_1_q[3]), .reset(and_3_out));  // open: Qn, preset
  T_Flip_Flop t_ff_16 (.T(1'b1), .clk(t_ff_12_qn), .Q(t_ff_2_q[3]), .reset(and_4_out));  // open: Qn, preset
  T_Flip_Flop t_ff_17 (.T(1'b1), .clk(t_ff_13_qn), .Q(t_ff_3_q[3]), .reset(and_5_out));  // open: Qn, preset
  T_Flip_Flop t_ff_18 (.T(1'b1), .clk(t_ff_14_qn), .Q(t_ff_4_q[3]), .reset(or_2_out));  // open: Qn, preset
  and and_1 (and_1_out, t_ff_5_q[0], t_ff_5_q[1]);
  and and_2 (and_2_out, T0_q[1], T0_q[3]);
  and and_3 (and_3_out, t_ff_1_q[1], t_ff_1_q[2]);
  and and_4 (and_4_out, t_ff_2_q[1], t_ff_2_q[3]);
  and and_5 (and_5_out, t_ff_3_q[1], t_ff_3_q[2]);
  and and_6 (and_6_out, t_ff_5_q[1], or_1_out);
  or or_1 (or_1_out, t_ff_4_q[3], t_ff_4_q[2]);
  and and_7 (and_7_out, t_ff_4_q[1], t_ff_4_q[3]);
  or or_2 (or_2_out, and_6_out, and_7_out);
  // BCD_to_7_Segment_decoder bcd_to_7_segment_decoder_1: pin names not known
  // BCD_to_7_Segment_decoder bcd_to_7_segment_decoder_2: pin names not known; wires that end beside it: T0_q
  // BCD_to_7_Segment_decoder bcd_to_7_segment_decoder_3: pin names not known; wires that end beside it: t_ff_1_q
  // BCD_to_7_Segment_decoder bcd_to_7_segment_decoder_4: pin names not known; wires that end beside it: t_ff_2_q
  // BCD_to_7_Segment_decoder bcd_to_7_segment_decoder_5: pin names not known; wires that end beside it: t_ff_3_q
  // BCD_to_7_Segment_decoder bcd_to_7_segment_decoder_6: pin names not known; wires that end beside it: t_ff_4_q, {2'b00, t_ff_5_q}

  assign {BOTTOM[24], BOTTOM[20], BOTTOM[16], BOTTOM[12], BOTTOM[8], BOTTOM[4:0]} = 10'h140;
  assign TOP[3:0] = 4'b0000;
endmodule

module countup (
  input  START,
  input  STOP,
  output [27:0] TOP,
  output [27:0] BOTTOM
);

  wire and_2_out, and_3_out, and_4_out, and_5_out, and_6_out, and_7_out, and_8_out, clock_1_out, clock_2_out,
       or_1_out, or_2_out, or_3_out, or_4_out, or_5_out, or_6_out, RESET, s_r_ff_1_q, s_r_ff_1_qn,
       s_r_ff_2_q, T0_qn, T1_qn, T2_qn, t_ff_1_qn, t_ff_2_qn, t_ff_3_qn, t_ff_4_qn, t_ff_5_qn, t_ff_6_qn,
       t_ff_7_qn, t_ff_8_qn, t_ff_9_qn, t_ff_10_qn, t_ff_11_qn, t_ff_12_qn, t_ff_13_qn, t_ff_14_qn,
       t_ff_15_qn;
  wire [3:0] T0_q, t_ff_1_q, t_ff_2_q, t_ff_3_q, t_ff_4_q, t_ff_5_q;

  Clock clock_1 (.out(clock_1_out));
  S_R_Flip_Flop #(.trigger("high")) s_r_ff_1 (
    .S(START), .R(STOP), .clk(1'b1), .Q(s_r_ff_1_q), .Qn(s_r_ff_1_qn));  // open: reset, preset
  S_R_Flip_Flop #(.trigger("falling")) s_r_ff_2 (
    .S(s_r_ff_1_qn), .R(s_r_ff_1_q), .clk(clock_2_out), .Q(s_r_ff_2_q), .reset(RESET));  // open: Qn, preset
  Clock clock_2 (.out(clock_2_out));
  and and_1 (RESET, s_r_ff_2_q, STOP);
  and and_2 (and_2_out, clock_1_out, s_r_ff_1_q);
  T_Flip_Flop T0 (.T(1'b1), .clk(and_2_out), .Q(T0_q[0]), .Qn(T0_qn), .reset(or_2_out));  // open: preset
  T_Flip_Flop t_ff_1 (.T(1'b1), .clk(or_2_out), .Q(t_ff_1_q[0]), .Qn(t_ff_1_qn), .reset(or_1_out));  // open: preset
  T_Flip_Flop t_ff_2 (.T(1'b1), .clk(or_1_out), .Q(t_ff_2_q[0]), .Qn(t_ff_2_qn), .reset(or_3_out));  // open: preset
  T_Flip_Flop t_ff_3 (.T(1'b1), .clk(or_3_out), .Q(t_ff_3_q[0]), .Qn(t_ff_3_qn), .reset(or_4_out));  // open: preset
  T_Flip_Flop t_ff_4 (.T(1'b1), .clk(or_4_out), .Q(t_ff_4_q[0]), .Qn(t_ff_4_qn), .reset(or_5_out));  // open: preset
  T_Flip_Flop t_ff_5 (.T(1'b1), .clk(or_5_out), .Q(t_ff_5_q[0]), .Qn(t_ff_5_qn), .reset(or_6_out));  // open: preset
  T_Flip_Flop T1 (.T(1'b1), .clk(T0_qn), .Q(T0_q[1]), .Qn(T1_qn), .reset(or_2_out));  // open: preset
  T_Flip_Flop t_ff_6 (.T(1'b1), .clk(t_ff_1_qn), .Q(t_ff_1_q[1]), .Qn(t_ff_6_qn), .reset(or_1_out));  // open: preset
  T_Flip_Flop t_ff_7 (.T(1'b1), .clk(t_ff_2_qn), .Q(t_ff_2_q[1]), .Qn(t_ff_7_qn), .reset(or_3_out));  // open: preset
  T_Flip_Flop t_ff_8 (.T(1'b1), .clk(t_ff_3_qn), .Q(t_ff_3_q[1]), .Qn(t_ff_8_qn), .reset(or_4_out));  // open: preset
  T_Flip_Flop t_ff_9 (.T(1'b1), .clk(t_ff_4_qn), .Q(t_ff_4_q[1]), .Qn(t_ff_9_qn), .reset(or_5_out));  // open: preset
  T_Flip_Flop t_ff_10 (.T(1'b1), .clk(t_ff_5_qn), .Q(t_ff_5_q[1]), .Qn(t_ff_10_qn), .reset(or_6_out));  // open: preset
  T_Flip_Flop T2 (.T(1'b1), .clk(T1_qn), .Q(T0_q[2]), .Qn(T2_qn), .reset(or_2_out));  // open: preset
  T_Flip_Flop t_ff_11 (.T(1'b1), .clk(t_ff_6_qn), .Q(t_ff_1_q[2]), .Qn(t_ff_11_qn), .reset(or_1_out));  // open: preset
  T_Flip_Flop t_ff_12 (.T(1'b1), .clk(t_ff_7_qn), .Q(t_ff_2_q[2]), .Qn(t_ff_12_qn), .reset(or_3_out));  // open: preset
  T_Flip_Flop t_ff_13 (.T(1'b1), .clk(t_ff_8_qn), .Q(t_ff_3_q[2]), .Qn(t_ff_13_qn), .reset(or_4_out));  // open: preset
  T_Flip_Flop t_ff_14 (.T(1'b1), .clk(t_ff_9_qn), .Q(t_ff_4_q[2]), .Qn(t_ff_14_qn), .reset(or_5_out));  // open: preset
  T_Flip_Flop t_ff_15 (.T(1'b1), .clk(t_ff_10_qn), .Q(t_ff_5_q[2]), .Qn(t_ff_15_qn), .reset(or_6_out));  // open: preset
  T_Flip_Flop T3 (.T(1'b1), .clk(T2_qn), .Q(T0_q[3]), .reset(or_2_out));  // open: Qn, preset
  T_Flip_Flop t_ff_16 (.T(1'b1), .clk(t_ff_11_qn), .Q(t_ff_1_q[3]), .reset(or_1_out));  // open: Qn, preset
  T_Flip_Flop t_ff_17 (.T(1'b1), .clk(t_ff_12_qn), .Q(t_ff_2_q[3]), .reset(or_3_out));  // open: Qn, preset
  T_Flip_Flop t_ff_18 (.T(1'b1), .clk(t_ff_13_qn), .Q(t_ff_3_q[3]), .reset(or_4_out));  // open: Qn, preset
  T_Flip_Flop t_ff_19 (.T(1'b1), .clk(t_ff_14_qn), .Q(t_ff_4_q[3]), .reset(or_5_out));  // open: Qn, preset
  T_Flip_Flop t_ff_20 (.T(1'b1), .clk(t_ff_15_qn), .Q(t_ff_5_q[3]), .reset(or_6_out));  // open: Qn, preset
  and and_3 (and_3_out, T0_q[1], T0_q[3]);
  and and_4 (and_4_out, t_ff_1_q[1], t_ff_1_q[2]);
  and and_5 (and_5_out, t_ff_2_q[1], t_ff_2_q[3]);
  and and_6 (and_6_out, t_ff_3_q[1], t_ff_3_q[2]);
  and and_7 (and_7_out, t_ff_4_q[1], t_ff_4_q[3]);
  and and_8 (and_8_out, t_ff_5_q[1], t_ff_5_q[3]);
  or or_1 (or_1_out, and_4_out, RESET);
  or or_2 (or_2_out, and_3_out, RESET);
  or or_3 (or_3_out, and_5_out, RESET);
  or or_4 (or_4_out, and_6_out, RESET);
  or or_5 (or_5_out, and_7_out, RESET);
  or or_6 (or_6_out, and_8_out, RESET);
  // BCD_to_7_Segment_decoder bcd_to_7_segment_decoder_1: pin names not known
  // BCD_to_7_Segment_decoder bcd_to_7_segment_decoder_2: pin names not known; wires that end beside it: T0_q
  // BCD_to_7_Segment_decoder bcd_to_7_segment_decoder_3: pin names not known; wires that end beside it: t_ff_1_q
  // BCD_to_7_Segment_decoder bcd_to_7_segment_decoder_4: pin names not known; wires that end beside it: t_ff_2_q
  // BCD_to_7_Segment_decoder bcd_to_7_segment_decoder_5: pin names not known; wires that end beside it: t_ff_3_q
  // BCD_to_7_Segment_decoder bcd_to_7_segment_decoder_6: pin names not known; wires that end beside it: t_ff_4_q, t_ff_5_q

  assign {BOTTOM[24], BOTTOM[20], BOTTOM[16], BOTTOM[12], BOTTOM[8], BOTTOM[4:0]} = 10'h140;
  assign TOP[3:0] = 4'b0000;
endmodule

module countdown (
  input  START,
  input  ADDS0,
  input  ADDS1,
  input  ADDM0,
  input  ADDM1,
  input  ADDH0,
  input  ADDH1,
  input  STOP,
  output [27:0] TOP,
  output [27:0] BOTTOM
);

  wire and_1_out, and_2_out, and_3_out, and_4_out, clock_1_out, clock_2_out, clock_3_out, clock_4_out,
       clock_5_out, clock_6_out, decoder_1_out15, H0_carry, M0_carry, M1_carry, multiplexer_1_out,
       multiplexer_2_out, multiplexer_3_out, multiplexer_4_out, multiplexer_5_out, multiplexer_6_out,
       multiplexer_7_out, multiplexer_8_out, multiplexer_9_out, multiplexer_10_out, multiplexer_11_out,
       S0_carry, S1_carry, SETUP, START_t, STOP_t;
  wire [3:0] H0, H1, M0, M1, nor_1_out, S0, S1;

  Multiplexer multiplexer_1 (.in0(S0_carry), .in1(1'b1), .out(multiplexer_1_out), .sel(SETUP));
  Multiplexer multiplexer_2 (.in0(ADDS1), .in1(clock_1_out), .out(multiplexer_2_out), .sel(START_t));
  Clock clock_1 (.out(clock_1_out));
  Multiplexer multiplexer_3 (.in0(and_1_out), .in1(1'b1), .out(multiplexer_3_out), .sel(SETUP));
  Multiplexer multiplexer_4 (.in0(ADDM0), .in1(clock_2_out), .out(multiplexer_4_out), .sel(START_t));
  Clock clock_2 (.out(clock_2_out));
  Multiplexer multiplexer_5 (.in0(and_2_out), .in1(1'b1), .out(multiplexer_5_out), .sel(SETUP));
  Multiplexer multiplexer_6 (.in0(ADDM1), .in1(clock_3_out), .out(multiplexer_6_out), .sel(START_t));
  Clock clock_3 (.out(clock_3_out));
  Clock clock_4 (.out(clock_4_out));
  Clock clock_5 (.out(clock_5_out));
  S_R_Flip_Flop #(.trigger("high")) s_r_ff_1 (
    .S(START), .R(STOP_t), .clk(1'b1), .Q(START_t), .Qn(SETUP));  // open: reset, preset
  Multiplexer multiplexer_7 (.in0(ADDS0), .in1(clock_6_out), .out(multiplexer_7_out), .sel(START_t));
  Clock clock_6 (.out(clock_6_out));
  Multiplexer multiplexer_8 (.in0(and_3_out), .in1(1'b1), .out(multiplexer_8_out), .sel(SETUP));
  Multiplexer multiplexer_9 (.in0(ADDH0), .in1(clock_4_out), .out(multiplexer_9_out), .sel(START_t));
  Multiplexer multiplexer_10 (.in0(and_4_out), .in1(1'b1), .out(multiplexer_10_out), .sel(SETUP));
  Multiplexer multiplexer_11 (.in0(ADDH1), .in1(clock_5_out), .out(multiplexer_11_out), .sel(START_t));
  Counter #(.max('h9), .width(4)) u_S0 (
    .clr(STOP), .up(SETUP), .count(1'b1), .clk(multiplexer_7_out), .carry(S0_carry), .Q(S0));  // open: load, D
  Counter #(.max('h5), .width(4)) u_S1 (
    .clr(STOP), .up(SETUP), .count(multiplexer_1_out), .clk(multiplexer_2_out), .carry(S1_carry), .Q(S1));  // open: load, D
  Counter #(.max('h9), .width(4)) u_M0 (
    .clr(STOP), .up(SETUP), .count(multiplexer_3_out), .clk(multiplexer_4_out), .carry(M0_carry), .Q(M0));  // open: load, D
  Counter #(.max('h5), .width(4)) u_M1 (
    .clr(STOP), .up(SETUP), .count(multiplexer_5_out), .clk(multiplexer_6_out), .carry(M1_carry), .Q(M1));  // open: load, D
  Counter #(.max('h9), .width(4)) u_H0 (
    .clr(STOP), .up(SETUP), .count(multiplexer_8_out), .clk(multiplexer_9_out), .carry(H0_carry), .Q(H0));  // open: load, D
  Counter #(.max('h9), .width(4)) u_H1 (
    .clr(STOP), .up(SETUP), .count(multiplexer_10_out), .clk(multiplexer_11_out), .Q(H1));  // open: load, D, carry
  Decoder #(.enable("false"), .select(4)) decoder_1 (
    .out15(decoder_1_out15), .sel(nor_1_out));  // open: out0, out1, out2, out3, out4, out5, out6, out7, out8, out9, out10, out11, out12, out13, out14
  assign nor_1_out = ~(S0 | S1 | M0 | M1 | H0 | H1);  // NOR_Gate nor_1, 4 bits wide
  or or_1 (STOP_t, decoder_1_out15, STOP);
  and and_1 (and_1_out, S1_carry, S0_carry);
  and and_2 (and_2_out, M0_carry, and_1_out);
  and and_3 (and_3_out, M1_carry, and_2_out);
  and and_4 (and_4_out, H0_carry, and_3_out);
  // BCD_to_7_Segment_decoder bcd_to_7_segment_decoder_1: pin names not known
  // BCD_to_7_Segment_decoder bcd_to_7_segment_decoder_2: pin names not known; wires that end beside it: S0
  // BCD_to_7_Segment_decoder bcd_to_7_segment_decoder_3: pin names not known; wires that end beside it: S1
  // BCD_to_7_Segment_decoder bcd_to_7_segment_decoder_4: pin names not known; wires that end beside it: M0
  // BCD_to_7_Segment_decoder bcd_to_7_segment_decoder_5: pin names not known; wires that end beside it: M1
  // BCD_to_7_Segment_decoder bcd_to_7_segment_decoder_6: pin names not known; wires that end beside it: H0, H1

  assign {BOTTOM[24], BOTTOM[20], BOTTOM[16], BOTTOM[12], BOTTOM[8], BOTTOM[4:0]} = 10'h140;
  assign TOP[3:0] = 4'b0000;

  // Other names for the same wires on the sheet: LOAD = START; RESET = STOP
endmodule

module alarmled (
  input  RESET,
  input  [27:0] TOPCLOCK,
  input  [27:0] TOPALARM,
  input  [27:0] BOTTOMALARM,
  input  [27:0] BOTTOMCLOCK,
  input  SET,
  input  [2:0] MODE,
  output LEDFLASH,
  output [2:0] alarmset
);

  wire and_1_out, and_2_out, and_3_out, and_4_out, clock_1_out, comparator_1_eq, comparator_2_eq,
       decoder_1_out2, or_1_out, or_2_out, s_r_ff_2_q, T0_qn, T1_q, T1_qn, T2_q, T2_qn, T3_q, T3_qn, t_ff_1_q;
  wire [55:0] multiplexer_1_out;

  Decoder #(.enable("false"), .select(3)) decoder_1 (
    .out2(decoder_1_out2), .sel(MODE));  // open: out0, out1, out3, out4, out5, out6, out7
  S_R_Flip_Flop #(.trigger("high")) s_r_ff_1 (
    .S(and_1_out), .R(or_2_out), .clk(1'b1), .Q(alarmset[2]));  // open: reset, Qn, preset
  and and_1 (and_1_out, decoder_1_out2, SET);
  Multiplexer #(.width(56)) multiplexer_1 (
    .in1({BOTTOMALARM, TOPALARM}), .out(multiplexer_1_out), .sel(alarmset[2]));  // open: in0
  Comparator #(.width(28)) comparator_1 (
    .a(TOPCLOCK), .b(multiplexer_1_out[27:0]), .eq(comparator_1_eq));  // open: gt, lt
  Comparator #(.width(28)) comparator_2 (
    .a(multiplexer_1_out[55:28]), .b(BOTTOMCLOCK), .eq(comparator_2_eq));  // open: gt, lt
  and and_2 (and_2_out, comparator_1_eq, comparator_2_eq);
  S_R_Flip_Flop #(.trigger("high")) s_r_ff_2 (
    .S(and_2_out), .R(or_2_out), .clk(1'b1), .Q(s_r_ff_2_q));  // open: reset, Qn, preset
  T_Flip_Flop #(.trigger("falling")) T0 (
    .T(s_r_ff_2_q), .clk(clock_1_out), .Q(LEDFLASH), .Qn(T0_qn), .reset(or_2_out));  // open: preset
  Clock clock_1 (.out(clock_1_out));
  T_Flip_Flop T1 (.T(1'b1), .clk(T0_qn), .Q(T1_q), .Qn(T1_qn), .reset(or_2_out));  // open: preset
  or or_1 (or_1_out, decoder_1_out2, LEDFLASH);
  T_Flip_Flop T2 (.T(1'b1), .clk(T1_qn), .Q(T2_q), .Qn(T2_qn), .reset(or_2_out));  // open: preset
  T_Flip_Flop T3 (.T(1'b1), .clk(T2_qn), .Q(T3_q), .Qn(T3_qn), .reset(or_2_out));  // open: preset
  and and_3 (and_3_out, RESET, or_1_out);
  T_Flip_Flop t_ff_1 (.T(1'b1), .clk(T3_qn), .Q(t_ff_1_q), .reset(or_2_out));  // open: Qn, preset
  or or_2 (or_2_out, and_4_out, and_3_out);
  and and_4 (and_4_out, t_ff_1_q, T1_q, T2_q, T3_q);

  assign alarmset[1:0] = {2{alarmset[2]}};
endmodule

module MOD10 (
  input  X,
  input  CLK,
  output [3:0] Q,
  output Overflow
);

  wire and_1_out, and_2_out, T0_qn, T1_qn, T2_qn;

  T_Flip_Flop T0 (.T(1'b1), .clk(CLK), .Q(Q[0]), .Qn(T0_qn), .reset(Overflow));  // open: preset
  T_Flip_Flop T1 (.T(1'b1), .clk(T0_qn), .Q(Q[1]), .Qn(T1_qn), .reset(Overflow));  // open: preset
  T_Flip_Flop T2 (.T(1'b1), .clk(T1_qn), .Q(Q[2]), .Qn(T2_qn), .reset(Overflow));  // open: preset
  T_Flip_Flop T3 (.T(1'b1), .clk(T2_qn), .Q(Q[3]), .reset(Overflow));  // open: Qn, preset
  and and_1 (and_1_out, X, Q[2]);
  and and_2 (and_2_out, Q[1], Q[3]);
  or or_1 (Overflow, and_1_out, and_2_out);
endmodule

module MOD10alt (
  input  X,
  input  CLK,
  output [3:0] Q,
  output Overflow
);

  wire and_1_out, and_2_out, T0_qn, T1_qn, T2_qn;

  T_Flip_Flop T0 (.T(1'b1), .clk(CLK), .Q(Q[0]), .Qn(T0_qn), .reset(Overflow));  // open: preset
  T_Flip_Flop T1 (.T(1'b1), .clk(T0_qn), .Q(Q[1]), .Qn(T1_qn), .reset(Overflow));  // open: preset
  T_Flip_Flop T2 (.T(1'b1), .clk(T1_qn), .Q(Q[2]), .Qn(T2_qn), .reset(Overflow));  // open: preset
  T_Flip_Flop T3 (.T(1'b1), .clk(T2_qn), .Q(Q[3]), .reset(Overflow));  // open: Qn, preset
  and and_1 (and_1_out, X, Q[1]);
  and and_2 (and_2_out, Q[1], Q[3]);
  or or_1 (Overflow, and_1_out, and_2_out);
endmodule

module MOD6 (
  input  CLK,
  output [3:0] Q,
  output Overflow
);

  wire T0_qn, T1_qn, T2_qn;

  T_Flip_Flop T0 (.T(1'b1), .clk(CLK), .Q(Q[0]), .Qn(T0_qn), .reset(Overflow));  // open: preset
  T_Flip_Flop T1 (.T(1'b1), .clk(T0_qn), .Q(Q[1]), .Qn(T1_qn), .reset(Overflow));  // open: preset
  T_Flip_Flop T2 (.T(1'b1), .clk(T1_qn), .Q(Q[2]), .Qn(T2_qn), .reset(Overflow));  // open: preset
  T_Flip_Flop T3 (.T(1'b1), .clk(T2_qn), .Q(Q[3]), .reset(Overflow));  // open: Qn, preset
  and and_1 (Overflow, Q[1], Q[2]);
endmodule

module MOD3 (
  input  CLK,
  output [3:0] Q,
  output Overflow
);

  wire and_1_out, T0_qn;

  T_Flip_Flop T0 (.T(1'b1), .clk(CLK), .Q(Q[0]), .Qn(T0_qn), .reset(and_1_out));  // open: preset
  T_Flip_Flop T1 (.T(1'b1), .clk(T0_qn), .Q(Overflow), .reset(and_1_out));  // open: Qn, preset
  and and_1 (and_1_out, Q[0], Overflow);

  assign Q[3:1] = {2'b00, Overflow};
endmodule

module MOD2 (
  input  CLK,
  output [3:0] Q,
  output OVERFLOW
);

  wire T0_qn, T1_q;

  T_Flip_Flop T0 (.T(1'b1), .clk(CLK), .Q(OVERFLOW), .Qn(T0_qn), .reset(T1_q));  // open: preset
  T_Flip_Flop T1 (.T(1'b1), .clk(T0_qn), .Q(T1_q), .reset(T1_q));  // open: Qn, preset

  assign Q = {3'b000, OVERFLOW};
endmodule
